# Fritzing sketch scheme (saved by Fritzing 0.9.3b)
breadboards: 1

parts:
  Part1 = SparkFun ESP8266 Thing  # not connected
  R1 = Photocell (LDR) [package=THT]
  DHT11_1 = DHT11 module  # not connected
  R2 = Resistor [tolerance=±5% resistance=10k package="1206 [SMD]"]

nets:
  N1: R1.pin_1, R2.Pin_1

notes:
  We use a different ESP8266 chip, you have to look at the source code for the data pins.

custom parts:
  DHT11 module: DHT11 black pcb module
